# Fritzing sketch SEN0114 (saved by Fritzing 0.9.4)

parts:
  パーツ1 = Arduino Nano (Rev3.0)
  パーツ2 = Soil Moisture Sensor

nets:
  GND: パーツ1.GND, パーツ2.GND
  N1: パーツ1.A5, パーツ2.SIG
  3V3: パーツ1.3V3, パーツ2.VCC
